// Logisim project p0-CRC.circ as structural Verilog: 2 circuits, main circuit CRC
module CRC (
  input  [7:0] A,
  input  [3:0] B,
  output [10:0] C
);

  wire [2:0] n4bit_mod2_1_c0, n4bit_mod2_2_c0, n4bit_mod2_3_c0, n4bit_mod2_4_c0, n4bit_mod2_5_c0,
       n4bit_mod2_6_c0, n4bit_mod2_7_c0;

  _4bit_mod2 u_4bit_mod2_1 (.A0(A[7:4]), .B0(B), .C0(n4bit_mod2_1_c0));  // open: D0
  _4bit_mod2 u_4bit_mod2_2 (.A0({n4bit_mod2_1_c0, A[3]}), .B0(B), .C0(n4bit_mod2_2_c0));  // open: D0
  _4bit_mod2 u_4bit_mod2_3 (.A0({n4bit_mod2_2_c0, A[2]}), .B0(B), .C0(n4bit_mod2_3_c0));  // open: D0
  _4bit_mod2 u_4bit_mod2_4 (.A0({n4bit_mod2_3_c0, A[1]}), .B0(B), .C0(n4bit_mod2_4_c0));  // open: D0
  _4bit_mod2 u_4bit_mod2_5 (.A0({n4bit_mod2_4_c0, A[0]}), .B0(B), .C0(n4bit_mod2_5_c0));  // open: D0
  _4bit_mod2 u_4bit_mod2_6 (.A0({n4bit_mod2_5_c0, 1'b0}), .B0(B), .C0(n4bit_mod2_6_c0));  // open: D0
  _4bit_mod2 u_4bit_mod2_7 (.A0({n4bit_mod2_6_c0, 1'b0}), .B0(B), .C0(n4bit_mod2_7_c0));  // open: D0
  _4bit_mod2 u_4bit_mod2_8 (.A0({n4bit_mod2_7_c0, 1'b0}), .B0(B), .C0(C[2:0]));  // open: D0

  assign C[10:3] = A;
endmodule

module _4bit_mod2 (
  input  [3:0] A0,
  input  [3:0] B0,
  output [2:0] C0,
  output D0
);

  wire [3:0] xor_1_out;

  assign xor_1_out = A0 ^ B0;  // XOR_Gate xor_1, 4 bits wide
  Multiplexer #(.width(3), .enable("false")) multiplexer_1 (.in0(A0[2:0]), .in1(xor_1_out[2:0]), .out(C0), .sel(A0[3]));

  assign D0 = A0[3];
endmodule
