// Logisim project p0-fsm.circ as structural Verilog: 3 circuits, main circuit fsm
module fsm (
  input  CLR,
  input  [1:0] in,
  output Z
);

  wire clock_1_out;
  wire [1:0] multiplexer_1_out, shift_1_next_state, state_q;

  shift shift_1 (.in(in), .curr_state(state_q), .next_state(shift_1_next_state));
  Multiplexer #(.width(2), .enable("false")) multiplexer_1 (
    .in0(shift_1_next_state), .in1(2'b00), .out(multiplexer_1_out), .sel(CLR));
  Register #(.width(2)) state (.D(multiplexer_1_out), .Q(state_q), .clk(clock_1_out));  // open: en, clr
  Clock clock_1 (.out(clock_1_out));
  \output  output_1 (.in(in), .curr_state(state_q), .Z(Z));
endmodule

module shift (
  input  [1:0] in,
  input  [1:0] curr_state,
  output [1:0] next_state
);

  wire and_1_out, and_2_out, and_3_out, and_4_out, and_5_out, and_6_out, and_7_out, and_8_out, not_1_out,
       not_2_out, not_3_out, not_4_out, not_5_out, not_6_out, not_7_out, not_8_out, not_9_out, not_10_out,
       not_11_out, not_12_out, not_13_out, not_14_out, not_15_out, not_16_out;

  not not_1 (not_1_out, in[1]);
  not not_2 (not_2_out, curr_state[1]);
  not not_3 (not_3_out, in[0]);
  not not_4 (not_4_out, curr_state[1]);
  not not_5 (not_5_out, in[1]);
  not not_6 (not_6_out, curr_state[0]);
  not not_7 (not_7_out, in[0]);
  not not_8 (not_8_out, curr_state[0]);
  not not_9 (not_9_out, in[0]);
  not not_10 (not_10_out, curr_state[1]);
  not not_11 (not_11_out, in[0]);
  not not_12 (not_12_out, curr_state[0]);
  not not_13 (not_13_out, in[1]);
  not not_14 (not_14_out, curr_state[1]);
  not not_15 (not_15_out, curr_state[0]);
  not not_16 (not_16_out, in[1]);
  and and_1 (and_1_out, not_1_out, not_2_out, curr_state[0]);
  and and_2 (and_2_out, not_3_out, not_4_out, curr_state[0]);
  and and_3 (and_3_out, not_5_out, curr_state[1], not_6_out);
  and and_4 (and_4_out, not_7_out, curr_state[1], not_8_out);
  and and_5 (and_5_out, not_9_out, not_10_out, curr_state[0]);
  and and_6 (and_6_out, not_11_out, curr_state[1], not_12_out);
  and and_7 (and_7_out, not_13_out, in[0], not_14_out, not_15_out);
  and and_8 (and_8_out, not_16_out, in[0], curr_state[1], curr_state[0]);
  or or_1 (next_state[1], and_1_out, and_2_out, and_3_out, and_4_out);
  or or_2 (next_state[0], and_5_out, and_6_out, and_7_out, and_8_out);

  // Notes on the sheet:
  //   状态码：0，没有有效位；1，有一位有效位；2，有两位有效位，但不能根据当前输入直接判断匹配；3，可以与当前输入直接判断匹配
endmodule

module \output  (
  input  [1:0] in,
  input  [1:0] curr_state,
  output Z
);

  wire comparator_1_eq, comparator_2_eq, comparator_3_eq, or_1_out;

  Comparator #(.width(2)) comparator_1 (.a(in), .b(2'b10), .eq(comparator_1_eq));  // open: gt, lt
  Comparator #(.width(2)) comparator_2 (.a(in), .b(2'b00), .eq(comparator_2_eq));  // open: gt, lt
  Comparator #(.width(2)) comparator_3 (.a(curr_state), .b(2'b11), .eq(comparator_3_eq));  // open: gt, lt
  or or_1 (or_1_out, comparator_1_eq, comparator_2_eq);
  and and_1 (Z, or_1_out, comparator_3_eq);
endmodule
