// Logisim project p0-ftoi.circ as structural Verilog: 2 circuits, main circuit ftoi
module ftoi (
  input  [15:0] float,
  output [31:0] \int 
);

  wire comparator_1_eq;
  wire [31:0] N_D_calculate_result;

  N_D_calculate N_D_calculate (.Sign(float[15]), .Exp(float[14:10]), .M(float[9:0]), .result(N_D_calculate_result));
  Comparator #(.width(5), .mode("unsigned")) comparator_1 (
    .a(float[14:10]), .b({5{1'b1}}), .eq(comparator_1_eq));  // open: gt, lt
  Multiplexer #(.width(32), .disabled(0), .enable("false")) multiplexer_1 (
    .in0(N_D_calculate_result), .in1({32{1'b0}}), .out(\int ), .sel(comparator_1_eq));

  // Notes on the sheet:
  //   处理后面两种情况
endmodule

module N_D_calculate (
  input  Sign,
  input  [4:0] Exp,
  input  [9:0] M,
  output [31:0] result
);

  wire comparator_1_eq, comparator_2_lt;
  wire [4:0] negator_1_out, subtractor_1_out;
  wire [31:0] adder_1_out, bit_extender_1_out, multiplexer_1_out, multiplexer_2_out, negator_2_out,
       shifter_1_out, shifter_2_out, shifter_3_out;

  assign bit_extender_1_out = {{22{1'b0}}, M};  // Bit_Extender bit_extender_1
  Subtractor #(.width(5)) subtractor_1 (.a(Exp), .b(5'b01111), .out(subtractor_1_out));  // open: bin, bout
  Adder #(.width(32)) adder_1 (.a(bit_extender_1_out), .b(32'h400), .out(adder_1_out));  // open: cin, cout
  Comparator #(.width(5)) comparator_1 (.a(Exp), .b({5{1'b0}}), .eq(comparator_1_eq));  // open: gt, lt
  Multiplexer #(.width(32), .disabled(0), .enable("false")) multiplexer_1 (
    .in0(adder_1_out), .in1(bit_extender_1_out), .out(multiplexer_1_out), .sel(comparator_1_eq));
  Negator #(.width(5)) negator_1 (.in(subtractor_1_out), .out(negator_1_out));
  Shifter #(.width(32), .shift("lr")) shifter_1 (.in(multiplexer_1_out), .\dist (negator_1_out), .out(shifter_1_out));
  Comparator #(.width(5)) comparator_2 (.a(subtractor_1_out), .b({5{1'b0}}), .lt(comparator_2_lt));  // open: gt, eq
  Shifter #(.width(32)) shifter_2 (.in(multiplexer_1_out), .\dist (subtractor_1_out), .out(shifter_2_out));
  Multiplexer #(.width(32), .disabled(0), .enable("false")) multiplexer_2 (
    .in0(shifter_2_out), .in1(shifter_1_out), .out(multiplexer_2_out), .sel(comparator_2_lt));
  Shifter #(.width(32), .shift("lr")) shifter_3 (.in(multiplexer_2_out), .\dist (5'b01010), .out(shifter_3_out));
  Multiplexer #(.width(32), .disabled(0), .enable("false")) multiplexer_3 (
    .in0(shifter_3_out), .in1(negator_2_out), .out(result), .sel(Sign));
  Negator #(.width(32)) negator_2 (.in(shifter_3_out), .out(negator_2_out));

  // Notes on the sheet:
  //   Exp经过减去01111得到E
  //   Exp=0,属于Denormalized情况，M无需在第10位置1；反之，则需要
  //   这是处理前两种情况的电路
  //   根据Exp与0的大小关系判断第10位是否置1
  //   E<0,则需要右移，且需要取反后传入移位器
  //   E>0，左移
  //   根据E与0的大小确定是左移还是右移
  //   符号位处理
  //   M的10位数位实际上都是小数部分，这里要进行处理
endmodule
