// Logisim project p0-grf.circ as structural Verilog: 1 circuit, main circuit grf
module grf (
  input  clk,
  input  reset,
  input  WE,
  input  [4:0] A1,
  input  [4:0] A2,
  input  [4:0] A3,
  input  [31:0] WD,
  output [31:0] RD1,
  output [31:0] RD2
);

  wire _0, _1, _2, _3, _4, _5, _6, _7, _8, _9, _10, _11, _12, _13, _14, _15, _16, _17, _18, _19, _20, _21,
       _22, _23, _24, _25, _26, _27, _28, _29, _30, _31;
  wire [31:0] _0_out, _1_in, _1_out, _2_in, _2_out, _3_in, _3_out, _4_in, _4_out, _5_in, _5_out, _6_in,
       _6_out, _7_in, _7_out, _8_in, _8_out, _9_in, _9_out, _10_in, _10_out, _11_in, _11_out, _12_in,
       _12_out, _13_in, _13_out, _14_in, _14_out, _15_in, _15_out, _16_in, _16_out, _17_in, _17_out, _18_in,
       _18_out, _19_in, _19_out, _20_in, _20_out, _21_in, _21_out, _22_in, _22_out, _23_in, _23_out, _24_in,
       _24_out, _25_in, _25_out, _26_in, _26_out, _27_in, _27_out, _28_in, _28_out, _29_in, _29_out, _30_in,
       _30_out, _31_in, _31_out;

  Register #(.width(32)) register_1 (.D({32{1'b0}}), .en(_0), .Q(_0_out), .clk(clk), .clr(reset));
  Register #(.width(32)) register_2 (.D(_1_in), .en(_1), .Q(_1_out), .clk(clk), .clr(reset));
  Register #(.width(32)) register_3 (.D(_2_in), .en(_2), .Q(_2_out), .clk(clk), .clr(reset));
  Register #(.width(32)) register_4 (.D(_3_in), .en(_3), .Q(_3_out), .clk(clk), .clr(reset));
  Register #(.width(32)) register_5 (.D(_4_in), .en(_4), .Q(_4_out), .clk(clk), .clr(reset));
  Register #(.width(32)) register_6 (.D(_5_in), .en(_5), .Q(_5_out), .clk(clk), .clr(reset));
  Register #(.width(32)) register_7 (.D(_6_in), .en(_6), .Q(_6_out), .clk(clk), .clr(reset));
  Register #(.width(32)) register_8 (.D(_7_in), .en(_7), .Q(_7_out), .clk(clk), .clr(reset));
  Register #(.width(32)) register_9 (.D(_8_in), .en(_8), .Q(_8_out), .clk(clk), .clr(reset));
  Register #(.width(32)) register_10 (.D(_9_in), .en(_9), .Q(_9_out), .clk(clk), .clr(reset));
  Register #(.width(32)) register_11 (.D(_10_in), .en(_10), .Q(_10_out), .clk(clk), .clr(reset));
  Register #(.width(32)) register_12 (.D(_11_in), .en(_11), .Q(_11_out), .clk(clk), .clr(reset));
  Register #(.width(32)) register_13 (.D(_12_in), .en(_12), .Q(_12_out), .clk(clk), .clr(reset));
  Register #(.width(32)) register_14 (.D(_13_in), .en(_13), .Q(_13_out), .clk(clk), .clr(reset));
  Register #(.width(32)) register_15 (.D(_14_in), .en(_14), .Q(_14_out), .clk(clk), .clr(reset));
  Register #(.width(32)) register_16 (.D(_15_in), .en(_15), .Q(_15_out), .clk(clk), .clr(reset));
  Register #(.width(32)) register_17 (.D(_16_in), .en(_16), .Q(_16_out), .clk(clk), .clr(reset));
  Register #(.width(32)) register_18 (.D(_17_in), .en(_17), .Q(_17_out), .clk(clk), .clr(reset));
  Register #(.width(32)) register_19 (.D(_18_in), .en(_18), .Q(_18_out), .clk(clk), .clr(reset));
  Register #(.width(32)) register_20 (.D(_19_in), .en(_19), .Q(_19_out), .clk(clk), .clr(reset));
  Register #(.width(32)) register_21 (.D(_20_in), .en(_20), .Q(_20_out), .clk(clk), .clr(reset));
  Register #(.width(32)) register_22 (.D(_21_in), .en(_21), .Q(_21_out), .clk(clk), .clr(reset));
  Register #(.width(32)) register_23 (.D(_22_in), .en(_22), .Q(_22_out), .clk(clk), .clr(reset));
  Register #(.width(32)) register_24 (.D(_23_in), .en(_23), .Q(_23_out), .clk(clk), .clr(reset));
  Register #(.width(32)) register_25 (.D(_24_in), .en(_24), .Q(_24_out), .clk(clk), .clr(reset));
  Register #(.width(32)) register_26 (.D(_25_in), .en(_25), .Q(_25_out), .clk(clk), .clr(reset));
  Register #(.width(32)) register_27 (.D(_26_in), .en(_26), .Q(_26_out), .clk(clk), .clr(reset));
  Register #(.width(32)) register_28 (.D(_27_in), .en(_27), .Q(_27_out), .clk(clk), .clr(reset));
  Register #(.width(32)) register_29 (.D(_28_in), .en(_28), .Q(_28_out), .clk(clk), .clr(reset));
  Register #(.width(32)) register_30 (.D(_29_in), .en(_29), .Q(_29_out), .clk(clk), .clr(reset));
  Register #(.width(32)) register_31 (.D(_30_in), .en(_30), .Q(_30_out), .clk(clk), .clr(reset));
  Register #(.width(32)) register_32 (.D(_31_in), .en(_31), .Q(_31_out), .clk(clk), .clr(reset));
  Demultiplexer #(.select(5), .width(32), .disabled(0), .enable("false")) demultiplexer_1 (
    .out1(_1_in), .out2(_2_in), .out3(_3_in), .out4(_4_in), .out5(_5_in), .out6(_6_in), .out7(_7_in),
    .out8(_8_in), .out9(_9_in), .out10(_10_in), .out11(_11_in), .out12(_12_in), .out13(_13_in),
    .out14(_14_in), .out15(_15_in), .out16(_16_in), .out17(_17_in), .out18(_18_in), .out19(_19_in),
    .out20(_20_in), .out21(_21_in), .out22(_22_in), .out23(_23_in), .out24(_24_in), .out25(_25_in),
    .out26(_26_in), .out27(_27_in), .out28(_28_in), .out29(_29_in), .out30(_30_in), .out31(_31_in), .in(WD),
    .sel(A3));  // open: out0
  Demultiplexer #(.select(5), .disabled(0), .enable("false")) demultiplexer_2 (
    .out0(_0), .out1(_1), .out2(_2), .out3(_3), .out4(_4), .out5(_5), .out6(_6), .out7(_7), .out8(_8),
    .out9(_9), .out10(_10), .out11(_11), .out12(_12), .out13(_13), .out14(_14), .out15(_15), .out16(_16),
    .out17(_17), .out18(_18), .out19(_19), .out20(_20), .out21(_21), .out22(_22), .out23(_23), .out24(_24),
    .out25(_25), .out26(_26), .out27(_27), .out28(_28), .out29(_29), .out30(_30), .out31(_31), .in(WE),
    .sel(A3));
  Multiplexer #(.select(5), .width(32), .disabled(0), .enable("false")) multiplexer_1 (
    .in0(_0_out), .in1(_1_out), .in2(_2_out), .in3(_3_out), .in4(_4_out), .in5(_5_out), .in6(_6_out),
    .in7(_7_out), .in8(_8_out), .in9(_9_out), .in10(_10_out), .in11(_11_out), .in12(_12_out), .in13(_13_out),
    .in14(_14_out), .in15(_15_out), .in16(_16_out), .in17(_17_out), .in18(_18_out), .in19(_19_out),
    .in20(_20_out), .in21(_21_out), .in22(_22_out), .in23(_23_out), .in24(_24_out), .in25(_25_out),
    .in26(_26_out), .in27(_27_out), .in28(_28_out), .in29(_29_out), .in30(_30_out), .in31(_31_out),
    .out(RD1), .sel(A1));
  Multiplexer #(.select(5), .width(32), .disabled(0), .enable("false")) multiplexer_2 (
    .in0(_0_out), .in1(_1_out), .in2(_2_out), .in3(_3_out), .in4(_4_out), .in5(_5_out), .in6(_6_out),
    .in7(_7_out), .in8(_8_out), .in9(_9_out), .in10(_10_out), .in11(_11_out), .in12(_12_out), .in13(_13_out),
    .in14(_14_out), .in15(_15_out), .in16(_16_out), .in17(_17_out), .in18(_18_out), .in19(_19_out),
    .in20(_20_out), .in21(_21_out), .in22(_22_out), .in23(_23_out), .in24(_24_out), .in25(_25_out),
    .in26(_26_out), .in27(_27_out), .in28(_28_out), .in29(_29_out), .in30(_30_out), .in31(_31_out),
    .out(RD2), .sel(A2));
endmodule
