// Logisim project p3-cpu-test.circ as structural Verilog: 10 circuits, main circuit main
module test (
  output [31:0] out_1,
  output [31:0] out_2,
  output out_3,
  output out_4,
  output [4:0] out_5,
  output [31:0] out_6,
  output halt,
  output [31:0] out_8,
  output [31:0] out_9
);

  wire clock_1_out, comparator_1_gt;
  wire [15:0] counter_1_q;

  Clock clock_1 (.out(clock_1_out));
  Counter #(.width(16), .max('hffff), .ongoal("stay")) counter_1 (
    .Q(counter_1_q), .carry(halt), .clk(clock_1_out));  // open: load, D, count, clr
  Comparator #(.width(16), .mode("unsigned")) comparator_1 (
    .a(16'h4), .b(counter_1_q), .gt(comparator_1_gt));  // open: eq, lt
  main main_1 (
    .reset(comparator_1_gt), .Instr(out_1), .pc(out_2), .RegWrite(out_3), .RegAddr(out_5), .RegData(out_6),
    .MemWrite(out_4), .MemAddr(out_8), .MemData(out_9));
endmodule

module main (
  input  reset,
  output [31:0] Instr,
  output [31:0] pc,
  output RegWrite,
  output [4:0] RegAddr,
  output [31:0] RegData,
  output MemWrite,
  output [31:0] MemAddr,
  output [31:0] MemData
);

  wire aluSrc, clk, extOp, memRead, regDst, zero;
  wire [1:0] memToR;
  wire [2:0] aluOp, jumpOp;
  wire [4:0] Splitter_rd, Splitter_rs, Splitter_rt;
  wire [5:0] Splitter_fn, Splitter_op;
  wire [31:0] DM_rd, EXT_output, GRF_rd1, multiplexer_2_out;
  wire [31:16] Splitter_imm_16;

  Clock clock_1 (.out(clk));
  IFU IFU (.offset(Splitter_imm_16), .nInstr(Instr), .zero(zero), .clk(clk), .reset(reset), .jumpOp(jumpOp), .pc(pc));
  Splitter Splitter (
    .instr(Instr), .fn(Splitter_fn), .rd(Splitter_rd), .rt(Splitter_rt), .rs(Splitter_rs), .op(Splitter_op),
    .imm_16(Splitter_imm_16));  // open: sh, addr_26
  Multiplexer #(.width(5), .enable("false")) multiplexer_1 (
    .in0(Splitter_rt), .in1(Splitter_rd), .out(RegAddr), .sel(regDst));
  Controller Controller (
    .op(Splitter_op), .fn(Splitter_fn), .regDst(regDst), .aluSrc(aluSrc), .aluOp(aluOp), .memToR(memToR),
    .memWrite(MemWrite), .memRead(memRead), .regWrite(RegWrite), .extOp(extOp), .jumpOp(jumpOp));
  EXT EXT (.\input (Splitter_imm_16), .\output (EXT_output), .extOp(extOp));
  GRF GRF (
    .A1(Splitter_rs), .A2(Splitter_rt), .A3(RegAddr), .WD(RegData), .RD1(GRF_rd1), .RD2(MemData), .clk(clk),
    .reset(reset), .WE(RegWrite));
  Multiplexer #(.width(32), .enable("false")) multiplexer_2 (
    .in0(MemData), .in1(EXT_output), .out(multiplexer_2_out), .sel(aluSrc));
  ALU ALU (.A(GRF_rd1), .B(multiplexer_2_out), .R(MemAddr), .zero(zero), .aluOp(aluOp));
  DM DM (.A(MemAddr[13:2]), .WD(MemData), .RD(DM_rd), .WE(MemWrite), .clk(clk), .RE(memRead), .reset(reset));
  Multiplexer #(.select(2), .width(32), .enable("false")) multiplexer_3 (
    .in0(MemAddr), .in1({Splitter_imm_16, {16{1'b0}}}), .in2(DM_rd), .out(RegData), .sel(memToR));  // open: in3
endmodule

module GRF (
  input  clk,
  input  reset,
  input  WE,
  input  [4:0] A1,
  input  [4:0] A2,
  input  [4:0] A3,
  input  [31:0] WD,
  output [31:0] RD1,
  output [31:0] RD2
);

  wire _0, _1, _2, _3, _4, _5, _6, _7, _8, _9, _10, _11, _12, _13, _14, _15, _16, _17, _18, _19, _20, _21,
       _22, _23, _24, _25, _26, _27, _28, _29, _30, _31;
  wire [31:0] _0_out, _1_in, _1_out, _2_in, _2_out, _3_in, _3_out, _4_in, _4_out, _5_in, _5_out, _6_in,
       _6_out, _7_in, _7_out, _8_in, _8_out, _9_in, _9_out, _10_in, _10_out, _11_in, _11_out, _12_in,
       _12_out, _13_in, _13_out, _14_in, _14_out, _15_in, _15_out, _16_in, _16_out, _17_in, _17_out, _18_in,
       _18_out, _19_in, _19_out, _20_in, _20_out, _21_in, _21_out, _22_in, _22_out, _23_in, _23_out, _24_in,
       _24_out, _25_in, _25_out, _26_in, _26_out, _27_in, _27_out, _28_in, _28_out, _29_in, _29_out, _30_in,
       _30_out, _31_in, _31_out;

  Register #(.width(32)) register_1 (.D({32{1'b0}}), .en(_0), .Q(_0_out), .clk(clk), .clr(reset));
  Register #(.width(32)) register_2 (.D(_1_in), .en(_1), .Q(_1_out), .clk(clk), .clr(reset));
  Register #(.width(32)) register_3 (.D(_2_in), .en(_2), .Q(_2_out), .clk(clk), .clr(reset));
  Register #(.width(32)) register_4 (.D(_3_in), .en(_3), .Q(_3_out), .clk(clk), .clr(reset));
  Register #(.width(32)) register_5 (.D(_4_in), .en(_4), .Q(_4_out), .clk(clk), .clr(reset));
  Register #(.width(32)) register_6 (.D(_5_in), .en(_5), .Q(_5_out), .clk(clk), .clr(reset));
  Register #(.width(32)) register_7 (.D(_6_in), .en(_6), .Q(_6_out), .clk(clk), .clr(reset));
  Register #(.width(32)) register_8 (.D(_7_in), .en(_7), .Q(_7_out), .clk(clk), .clr(reset));
  Register #(.width(32)) register_9 (.D(_8_in), .en(_8), .Q(_8_out), .clk(clk), .clr(reset));
  Register #(.width(32)) register_10 (.D(_9_in), .en(_9), .Q(_9_out), .clk(clk), .clr(reset));
  Register #(.width(32)) register_11 (.D(_10_in), .en(_10), .Q(_10_out), .clk(clk), .clr(reset));
  Register #(.width(32)) register_12 (.D(_11_in), .en(_11), .Q(_11_out), .clk(clk), .clr(reset));
  Register #(.width(32)) register_13 (.D(_12_in), .en(_12), .Q(_12_out), .clk(clk), .clr(reset));
  Register #(.width(32)) register_14 (.D(_13_in), .en(_13), .Q(_13_out), .clk(clk), .clr(reset));
  Register #(.width(32)) register_15 (.D(_14_in), .en(_14), .Q(_14_out), .clk(clk), .clr(reset));
  Register #(.width(32)) register_16 (.D(_15_in), .en(_15), .Q(_15_out), .clk(clk), .clr(reset));
  Register #(.width(32)) register_17 (.D(_16_in), .en(_16), .Q(_16_out), .clk(clk), .clr(reset));
  Register #(.width(32)) register_18 (.D(_17_in), .en(_17), .Q(_17_out), .clk(clk), .clr(reset));
  Register #(.width(32)) register_19 (.D(_18_in), .en(_18), .Q(_18_out), .clk(clk), .clr(reset));
  Register #(.width(32)) register_20 (.D(_19_in), .en(_19), .Q(_19_out), .clk(clk), .clr(reset));
  Register #(.width(32)) register_21 (.D(_20_in), .en(_20), .Q(_20_out), .clk(clk), .clr(reset));
  Register #(.width(32)) register_22 (.D(_21_in), .en(_21), .Q(_21_out), .clk(clk), .clr(reset));
  Register #(.width(32)) register_23 (.D(_22_in), .en(_22), .Q(_22_out), .clk(clk), .clr(reset));
  Register #(.width(32)) register_24 (.D(_23_in), .en(_23), .Q(_23_out), .clk(clk), .clr(reset));
  Register #(.width(32)) register_25 (.D(_24_in), .en(_24), .Q(_24_out), .clk(clk), .clr(reset));
  Register #(.width(32)) register_26 (.D(_25_in), .en(_25), .Q(_25_out), .clk(clk), .clr(reset));
  Register #(.width(32)) register_27 (.D(_26_in), .en(_26), .Q(_26_out), .clk(clk), .clr(reset));
  Register #(.width(32)) register_28 (.D(_27_in), .en(_27), .Q(_27_out), .clk(clk), .clr(reset));
  Register #(.width(32)) register_29 (.D(_28_in), .en(_28), .Q(_28_out), .clk(clk), .clr(reset));
  Register #(.width(32)) register_30 (.D(_29_in), .en(_29), .Q(_29_out), .clk(clk), .clr(reset));
  Register #(.width(32)) register_31 (.D(_30_in), .en(_30), .Q(_30_out), .clk(clk), .clr(reset));
  Register #(.width(32)) register_32 (.D(_31_in), .en(_31), .Q(_31_out), .clk(clk), .clr(reset));
  Demultiplexer #(.select(5), .width(32), .disabled(0), .enable("false")) demultiplexer_1 (
    .out1(_1_in), .out2(_2_in), .out3(_3_in), .out4(_4_in), .out5(_5_in), .out6(_6_in), .out7(_7_in),
    .out8(_8_in), .out9(_9_in), .out10(_10_in), .out11(_11_in), .out12(_12_in), .out13(_13_in),
    .out14(_14_in), .out15(_15_in), .out16(_16_in), .out17(_17_in), .out18(_18_in), .out19(_19_in),
    .out20(_20_in), .out21(_21_in), .out22(_22_in), .out23(_23_in), .out24(_24_in), .out25(_25_in),
    .out26(_26_in), .out27(_27_in), .out28(_28_in), .out29(_29_in), .out30(_30_in), .out31(_31_in), .in(WD),
    .sel(A3));  // open: out0
  Demultiplexer #(.select(5), .disabled(0), .enable("false")) demultiplexer_2 (
    .out0(_0), .out1(_1), .out2(_2), .out3(_3), .out4(_4), .out5(_5), .out6(_6), .out7(_7), .out8(_8),
    .out9(_9), .out10(_10), .out11(_11), .out12(_12), .out13(_13), .out14(_14), .out15(_15), .out16(_16),
    .out17(_17), .out18(_18), .out19(_19), .out20(_20), .out21(_21), .out22(_22), .out23(_23), .out24(_24),
    .out25(_25), .out26(_26), .out27(_27), .out28(_28), .out29(_29), .out30(_30), .out31(_31), .in(WE),
    .sel(A3));
  Multiplexer #(.select(5), .width(32), .disabled(0), .enable("false")) multiplexer_1 (
    .in0(_0_out), .in1(_1_out), .in2(_2_out), .in3(_3_out), .in4(_4_out), .in5(_5_out), .in6(_6_out),
    .in7(_7_out), .in8(_8_out), .in9(_9_out), .in10(_10_out), .in11(_11_out), .in12(_12_out), .in13(_13_out),
    .in14(_14_out), .in15(_15_out), .in16(_16_out), .in17(_17_out), .in18(_18_out), .in19(_19_out),
    .in20(_20_out), .in21(_21_out), .in22(_22_out), .in23(_23_out), .in24(_24_out), .in25(_25_out),
    .in26(_26_out), .in27(_27_out), .in28(_28_out), .in29(_29_out), .in30(_30_out), .in31(_31_out),
    .out(RD1), .sel(A1));
  Multiplexer #(.select(5), .width(32), .disabled(0), .enable("false")) multiplexer_2 (
    .in0(_0_out), .in1(_1_out), .in2(_2_out), .in3(_3_out), .in4(_4_out), .in5(_5_out), .in6(_6_out),
    .in7(_7_out), .in8(_8_out), .in9(_9_out), .in10(_10_out), .in11(_11_out), .in12(_12_out), .in13(_13_out),
    .in14(_14_out), .in15(_15_out), .in16(_16_out), .in17(_17_out), .in18(_18_out), .in19(_19_out),
    .in20(_20_out), .in21(_21_out), .in22(_22_out), .in23(_23_out), .in24(_24_out), .in25(_25_out),
    .in26(_26_out), .in27(_27_out), .in28(_28_out), .in29(_29_out), .in30(_30_out), .in31(_31_out),
    .out(RD2), .sel(A2));
endmodule

module EXT (
  input  [15:0] \input ,
  input  extOp,
  output [31:0] \output 
);

  wire [31:0] bit_extender_1_out, bit_extender_2_out;

  assign bit_extender_1_out = {{16{1'b0}}, \input };  // Bit_Extender bit_extender_1
  assign bit_extender_2_out = {{16{\input [15]}}, \input };  // Bit_Extender bit_extender_2
  Multiplexer #(.width(32), .enable("false")) multiplexer_1 (
    .in0(bit_extender_1_out), .in1(bit_extender_2_out), .out(\output ), .sel(extOp));
endmodule

module ALU (
  input  [31:0] A,
  input  [31:0] B,
  input  [2:0] aluOp,
  output [31:0] R,
  output zero
);

  wire [31:0] adder_1_out, and_1_out, or_1_out, subtractor_1_out;

  Adder #(.width(32)) adder_1 (.a(A), .b(B), .out(adder_1_out));  // open: cin, cout
  Subtractor #(.width(32)) subtractor_1 (.a(A), .b(B), .out(subtractor_1_out));  // open: bin, bout
  assign and_1_out = A & B;  // AND_Gate and_1, 32 bits wide
  assign or_1_out = A | B;  // OR_Gate or_1, 32 bits wide
  Comparator #(.width(32)) comparator_1 (.a(A), .b(B), .eq(zero));  // open: gt, lt
  Multiplexer #(.select(3), .width(32), .enable("false")) multiplexer_1 (
    .in0(adder_1_out), .in1(subtractor_1_out), .in2(and_1_out), .in3(or_1_out), .in4({32{1'b0}}), .out(R),
    .sel(aluOp));  // open: in5, in6, in7
endmodule

module DM (
  input  [11:0] A,
  input  WE,
  input  RE,
  input  [31:0] WD,
  input  reset,
  input  clk,
  output [31:0] RD
);

  RAM #(.addrWidth(12), .dataWidth(32), .bus("separate")) ram_1 (
    .addr(A), .din(WD), .data(RD), .str(WE), .clk(clk), .ld(RE), .clr(reset));  // open: sel
endmodule

module Splitter (
  input  [31:0] instr,
  output [5:0] fn,
  output [4:0] sh,
  output [4:0] rd,
  output [4:0] rt,
  output [4:0] rs,
  output [5:0] op,
  output [15:0] imm_16,
  output [25:0] addr_26
);

  Bit_Extender #(.in_width(32)) bit_extender_1 (.in(instr), .out(imm_16));
  Bit_Extender #(.in_width(32), .out_width(26)) bit_extender_2 (.in(instr), .out(addr_26));

  assign fn = instr[5:0];
  assign op = instr[31:26];
  assign rd = instr[15:11];
  assign rs = instr[25:21];
  assign rt = instr[20:16];
  assign sh = instr[10:6];
endmodule

module IFU (
  input  zero,
  input  [2:0] jumpOp,
  input  clk,
  input  reset,
  input  [15:0] offset,
  output [31:0] nInstr,
  output [31:0] pc
);

  wire comparator_1_eq;
  wire [31:0] adder_1_out, beq_nPC, bit_extender_1_out, nPC, offset_t, PC_4, PC_q, subtractor_1_out;

  Adder #(.width(32)) adder_1 (.a(PC_4), .b(offset_t), .out(adder_1_out));  // open: cin, cout
  Adder #(.width(32)) adder_2 (.a(pc), .b(32'h4), .out(PC_4));  // open: cin, cout
  assign bit_extender_1_out = {{16{offset[15]}}, offset};  // Bit_Extender bit_extender_1
  Multiplexer #(.width(32), .enable("false")) multiplexer_1 (.in0(PC_4), .in1(adder_1_out), .out(beq_nPC), .sel(zero));
  Shifter #(.width(32)) shifter_1 (.in(bit_extender_1_out), .\dist (5'b00010), .out(offset_t));
  Register #(.width(32)) u_PC (.D(nPC), .Q(PC_q), .clk(clk), .clr(reset));  // open: en
  Comparator #(.width(32)) comparator_1 (.a(PC_q), .b({32{1'b0}}), .eq(comparator_1_eq));  // open: gt, lt
  Multiplexer #(.width(32), .enable("false")) multiplexer_2 (
    .in0(PC_q), .in1(32'h3000), .out(pc), .sel(comparator_1_eq));
  Multiplexer #(.select(3), .width(32), .enable("false")) multiplexer_3 (
    .in0(PC_4), .in1(beq_nPC), .out(nPC), .sel(jumpOp));  // open: in2, in3, in4, in5, in6, in7
  Subtractor #(.width(32)) subtractor_1 (.a(pc), .b(32'h3000), .out(subtractor_1_out));  // open: bin, bout
  IM IM (.A(subtractor_1_out[13:2]), .nInstr(nInstr));

  // Notes on the sheet:
  //   beq处理
endmodule

module IM (
  input  [11:0] A,
  output [31:0] nInstr
);

  ROM #(.addrWidth(12), .dataWidth(32)) rom_1 (.addr(A), .data(nInstr));  // open: sel

  // Notes on the sheet:
  //   contents of rom_1 (hex, n*v repeats v):
  //   34090000 352a0005 340b0007 34040009 3405000d 12b4820 8b2020 ab2822 112a0002 12b4820 112a0000 12b4822
  //   3c0c0fff 3c0e0123 340a0004 ad4e0008 ad4c0014 8d4d0014 8d4f0008
endmodule

module Controller (
  input  [5:0] op,
  input  [5:0] fn,
  output regDst,
  output aluSrc,
  output [1:0] memToR,
  output memWrite,
  output memRead,
  output regWrite,
  output extOp,
  output [2:0] jumpOp,
  output [2:0] aluOp
);

  wire add, sub, sw;

  or or_1 (regDst, add, sub);
  or or_2 (aluSrc, aluOp[1], memToR[1], sw);
  and and_1 (aluOp[0], ~add, ~memToR[1], ~sw, ~aluOp[2]);  // AND_Gate
  and and_2 (add, ~op[0], ~op[1], ~op[2], ~op[3], ~op[4], ~op[5], ~fn[0], ~fn[1], ~fn[2], ~fn[3], ~fn[4], fn[5]);  // AND_Gate
  and and_3 (sub, ~op[0], ~op[1], ~op[2], ~op[3], ~op[4], ~op[5], ~fn[0], fn[1], ~fn[2], ~fn[3], ~fn[4], fn[5]);  // AND_Gate
  buf or_3 (memWrite, sw);  // OR_Gate
  buf or_4 (memRead, memToR[1]);  // OR_Gate
  and and_4 (aluOp[1], op[0], ~op[1], op[2], op[3], ~op[4], ~op[5]);  // AND_Gate
  and and_5 (memToR[1], op[0], op[1], ~op[2], ~op[3], ~op[4], op[5]);  // AND_Gate
  or or_5 (regWrite, add, sub, aluOp[1], memToR[1], memToR[0]);
  or or_6 (extOp, memToR[1], sw);
  assign jumpOp = {{2{1'b0}}, aluOp[2]};  // Bit_Extender bit_extender_1
  and and_6 (sw, op[0], op[1], ~op[2], op[3], ~op[4], op[5]);  // AND_Gate
  and and_7 (aluOp[2], ~op[0], ~op[1], op[2], ~op[3], ~op[4], ~op[5]);  // AND_Gate
  and and_8 (memToR[0], op[0], op[1], op[2], op[3], ~op[4], ~op[5]);  // AND_Gate

  // Other names for the same wires on the sheet: ori = aluOp[1]; beq = aluOp[2]; lui = memToR[0]; lw = memToR[1]

  // Notes on the sheet:
  //   或逻辑
  //   和逻辑
endmodule
