// Logisim project pre-2^nmod5.circ as structural Verilog: 3 circuits, main circuit mod5
module mod5 (
  input  In,
  output S0,
  output S1,
  output S2,
  output S3,
  output S4
);

  wire clock_1_out;
  wire [1:0] register_1_q, shift_1_i2_;

  shift shift_1 (.I1(register_1_q[1]), .I0(register_1_q[0]), .i(In), .I1_(shift_1_i2_[1]), .I2_(shift_1_i2_[0]));
  Register #(.width(2)) register_1 (.D(shift_1_i2_), .Q(register_1_q), .clk(clock_1_out));  // open: en, clr
  Clock clock_1 (.out(clock_1_out));
  shift shift_2 ();  // open: I1, I0, i, I1_, I2_
  \output  output_1 (.I1(register_1_q[1]), .I0(register_1_q[0]), .i(In), .S0(S0), .S1(S1), .S2(S2), .S3(S3), .S4(S4));
endmodule

module shift (
  input  I1,
  input  I0,
  input  i,
  output I1_,
  output I2_
);

  wire and_1_out, and_2_out, and_3_out, and_4_out, and_5_out, and_6_out, not_1_out, not_2_out, not_3_out,
       not_4_out, not_5_out, not_6_out, not_7_out, not_8_out;

  not not_1 (not_1_out, I1);
  not not_2 (not_2_out, I0);
  not not_3 (not_3_out, I1);
  not not_4 (not_4_out, I0);
  not not_5 (not_5_out, I1);
  not not_6 (not_6_out, i);
  not not_7 (not_7_out, I0);
  not not_8 (not_8_out, i);
  and and_1 (and_1_out, not_1_out, I0);
  and and_2 (and_2_out, I1, not_2_out);
  and and_3 (and_3_out, not_3_out, not_4_out, i);
  and and_4 (and_4_out, not_5_out, I0, not_6_out);
  and and_5 (and_5_out, I1, not_7_out, not_8_out);
  and and_6 (and_6_out, I1, I0, i);
  or or_1 (I1_, and_1_out, and_2_out);
  or or_2 (I2_, and_3_out, and_4_out, and_5_out, and_6_out);
endmodule

module \output  (
  input  I1,
  input  I0,
  input  i,
  output S0,
  output S1,
  output S2,
  output S3,
  output S4
);

  wire and_1_out, and_2_out, and_3_out, and_4_out, and_5_out, and_6_out, and_7_out, and_8_out, not_1_out,
       not_2_out, not_3_out, not_4_out, not_5_out, not_6_out, not_7_out, not_8_out, not_9_out, not_10_out,
       not_11_out, not_12_out;

  not not_1 (not_1_out, I1);
  not not_2 (not_2_out, I0);
  not not_3 (not_3_out, i);
  not not_4 (not_4_out, i);
  not not_5 (not_5_out, I1);
  not not_6 (not_6_out, I0);
  not not_7 (not_7_out, I1);
  not not_8 (not_8_out, I0);
  not not_9 (not_9_out, I1);
  not not_10 (not_10_out, i);
  not not_11 (not_11_out, I0);
  not not_12 (not_12_out, i);
  and and_1 (and_1_out, not_1_out, not_2_out, not_3_out);
  and and_2 (and_2_out, I1, I0, not_4_out);
  and and_3 (and_3_out, not_5_out, not_6_out, i);
  and and_4 (and_4_out, I1, I0, i);
  and and_5 (and_5_out, not_7_out, I0, i);
  and and_6 (and_6_out, I1, not_8_out, i);
  and and_7 (and_7_out, not_9_out, I0, not_10_out);
  and and_8 (and_8_out, I1, not_11_out, not_12_out);
  or or_1 (S1, and_1_out, and_2_out);
  or or_2 (S2, and_3_out, and_4_out);
  or or_3 (S3, and_5_out, and_6_out);
  or or_4 (S4, and_7_out, and_8_out);

  assign S0 = 1'b0;
endmodule
