// Logisim project pre-4bitsort.circ as structural Verilog: 4 circuits, main circuit 1bit_swap
module _4bit_sort (
  input  [3:0] A,
  input  [3:0] B,
  input  [3:0] C,
  input  [3:0] D,
  output [3:0] _1,
  output [3:0] _2,
  output [3:0] _3,
  output [3:0] _4
);

  wire [3:0] n4bit_largerswap_1_out_3, n4bit_largerswap_1_out_4, n4bit_largerswap_2_out_3,
       n4bit_largerswap_2_out_4, n4bit_largerswap_3_out_3, n4bit_largerswap_4_out_3,
       n4bit_largerswap_4_out_4, n4bit_largerswap_5_out_3;

  _4bit_largerswap u_4bit_largerswap_1 (
    .in_1(A), .in_2(B), .out_3(n4bit_largerswap_1_out_3), .out_4(n4bit_largerswap_1_out_4));
  _4bit_largerswap u_4bit_largerswap_2 (
    .in_1(n4bit_largerswap_1_out_4), .in_2(C), .out_3(n4bit_largerswap_2_out_3),
    .out_4(n4bit_largerswap_2_out_4));
  _4bit_largerswap u_4bit_largerswap_3 (
    .in_1(n4bit_largerswap_2_out_4), .in_2(D), .out_3(n4bit_largerswap_3_out_3), .out_4(_4));
  _4bit_largerswap u_4bit_largerswap_4 (
    .in_1(n4bit_largerswap_1_out_3), .in_2(n4bit_largerswap_2_out_3), .out_3(n4bit_largerswap_4_out_3),
    .out_4(n4bit_largerswap_4_out_4));
  _4bit_largerswap u_4bit_largerswap_5 (
    .in_1(n4bit_largerswap_4_out_4), .in_2(n4bit_largerswap_3_out_3), .out_3(n4bit_largerswap_5_out_3),
    .out_4(_3));
  _4bit_largerswap u_4bit_largerswap_6 (
    .in_1(n4bit_largerswap_4_out_3), .in_2(n4bit_largerswap_5_out_3), .out_3(_1), .out_4(_2));
endmodule

module _1bit_swap (
  input  I1,
  input  I2,
  input  S,
  output O1,
  output O2
);

  wire and_1_out, and_2_out, and_3_out, and_4_out, not_1_out, not_2_out;

  not not_1 (not_1_out, S);
  not not_2 (not_2_out, S);
  and and_1 (and_1_out, I1, not_1_out);
  and and_2 (and_2_out, I2, S);
  and and_3 (and_3_out, I1, S);
  and and_4 (and_4_out, I2, not_2_out);
  or or_1 (O1, and_1_out, and_2_out);
  or or_2 (O2, and_3_out, and_4_out);

  // Other names for the same wires on the sheet: in0 = S; in1 = I1; in2 = I2
endmodule

module _4bit_swap (
  input  in_1,
  input  [3:0] in_2,
  input  [3:0] in_3,
  output [3:0] out_4,
  output [3:0] out_5
);

  _1bit_swap u_1bit_swap_1 (.I1(in_2[0]), .I2(in_3[0]), .S(in_1), .O1(out_4[0]), .O2(out_5[0]));
  _1bit_swap u_1bit_swap_2 (.I1(in_2[1]), .I2(in_3[1]), .S(in_1), .O1(out_4[1]), .O2(out_5[1]));
  _1bit_swap u_1bit_swap_3 (.I1(in_2[2]), .I2(in_3[2]), .S(in_1), .O1(out_4[2]), .O2(out_5[2]));
  _1bit_swap u_1bit_swap_4 (.I1(in_2[3]), .I2(in_3[3]), .S(in_1), .O1(out_4[3]), .O2(out_5[3]));
endmodule

module _4bit_largerswap (
  input  [3:0] in_1,
  input  [3:0] in_2,
  output [3:0] out_3,
  output [3:0] out_4
);

  wire comparator_1_gt;

  Comparator #(.width(4), .mode("unsigned")) comparator_1 (.a(in_1), .b(in_2), .gt(comparator_1_gt));  // open: eq, lt
  _4bit_swap u_4bit_swap_1 (.in_2(in_1), .in_3(in_2), .out_4(out_3), .out_5(out_4), .in_1(comparator_1_gt));
endmodule
