// Logisim project pre-fibonacci_1.circ as structural Verilog: 3 circuits, main circuit main
module main (
  input  [2:0] N,
  output [3:0] Nth
);

  wire \output ;
  wire [3:0] result;

  count count (.\input (N), .\output (\output ));
  calculate calculate (.stop(\output ), .current(result));
  Multiplexer #(.width(4)) multiplexer_1 (.in0(4'b0000), .in1(result), .out(Nth), .sel(\output ));  // open: en
endmodule

module count (
  input  [2:0] \input ,
  output \output 
);

  wire clock;
  wire [3:0] bound, count;

  Clock clock_1 (.out(clock));
  assign bound = {{1{1'b0}}, \input };  // Bit_Extender bit_extender_1
  Counter #(.width(4), .max('hf), .ongoal("stay")) counter_1 (
    .Q(count), .clk(clock));  // open: load, D, count, carry, clr
  Comparator #(.width(4), .mode("unsigned")) comparator_1 (.a(bound), .b(count), .lt(\output ));  // open: gt, eq
endmodule

module calculate (
  input  stop,
  output [3:0] current
);

  wire clock, control, enable;
  wire [3:0] adder_1_out, multiplexer_1_out, previous;

  Clock clock_1 (.out(clock));
  not not_1 (enable, stop);
  Counter #(.width(1), .max('h1), .ongoal("stay")) init_control (
    .Q(control), .clk(clock));  // open: load, D, count, carry, clr
  Multiplexer #(.width(4)) multiplexer_1 (
    .in0(4'b0001), .in1(current), .out(multiplexer_1_out), .sel(control));  // open: en
  Adder #(.width(4)) adder_1 (.a(previous), .b(current), .out(adder_1_out));  // open: cin, cout
  Register #(.width(4)) u_previous (.D(multiplexer_1_out), .en(enable), .Q(previous), .clk(clock));  // open: clr
  Register #(.width(4)) u_current (.D(adder_1_out), .en(enable), .Q(current), .clk(clock));  // open: clr
endmodule
