// Logisim project pre-fibonacci_2.circ as structural Verilog: 8 circuits, main circuit main
module main (
  input  [31:0] N,
  output [31:0] Nth
);

  wire lowest, stop;

  count count_1 (.\input (N), .lowest(lowest), .stop(stop));
  calculate calculate_1 (.lowest(lowest), .stop(stop), .Nth(Nth));
endmodule

module matrix_memory (
  input  [31:0] a11_i,
  input  [31:0] a12_i,
  input  [31:0] a21_i,
  input  [31:0] a22_i,
  input  clock,
  input  enable,
  output [31:0] a11_o,
  output [31:0] a12_o,
  output [31:0] a21_o,
  output [31:0] a22_o
);

  Register #(.width(32)) a11 (.D(a11_i), .en(enable), .Q(a11_o), .clk(clock));  // open: clr
  Register #(.width(32)) a21 (.D(a21_i), .en(enable), .Q(a21_o), .clk(clock));  // open: clr
  Register #(.width(32)) a12 (.D(a12_i), .en(enable), .Q(a12_o), .clk(clock));  // open: clr
  Register #(.width(32)) a22 (.D(a22_i), .en(enable), .Q(a22_o), .clk(clock));  // open: clr
endmodule

module matrix_mul (
  input  [31:0] a11,
  input  [31:0] b11,
  input  [31:0] a12,
  input  [31:0] b12,
  input  [31:0] a21,
  input  [31:0] b21,
  input  [31:0] a22,
  input  [31:0] b22,
  output [31:0] r11,
  output [31:0] r12,
  output [31:0] r21,
  output [31:0] r22
);

  wire [31:0] multiplier_1_out, multiplier_2_out, multiplier_3_out, multiplier_4_out, multiplier_5_out,
       multiplier_6_out, multiplier_7_out, multiplier_8_out;

  Multiplier #(.width(32)) multiplier_1 (.a(a11), .b(b11), .out(multiplier_1_out));  // open: cin, cout
  Multiplier #(.width(32)) multiplier_2 (.a(a12), .b(b21), .out(multiplier_2_out));  // open: cin, cout
  Multiplier #(.width(32)) multiplier_3 (.a(a21), .b(b11), .out(multiplier_3_out));  // open: cin, cout
  Multiplier #(.width(32)) multiplier_4 (.a(a22), .b(b21), .out(multiplier_4_out));  // open: cin, cout
  Adder #(.width(32)) adder_1 (.a(multiplier_1_out), .b(multiplier_2_out), .out(r11));  // open: cin, cout
  Adder #(.width(32)) adder_2 (.a(multiplier_3_out), .b(multiplier_4_out), .out(r21));  // open: cin, cout
  Multiplier #(.width(32)) multiplier_5 (.a(a11), .b(b12), .out(multiplier_5_out));  // open: cin, cout
  Multiplier #(.width(32)) multiplier_6 (.a(a12), .b(b22), .out(multiplier_6_out));  // open: cin, cout
  Multiplier #(.width(32)) multiplier_7 (.a(a21), .b(b12), .out(multiplier_7_out));  // open: cin, cout
  Multiplier #(.width(32)) multiplier_8 (.a(a22), .b(b22), .out(multiplier_8_out));  // open: cin, cout
  Adder #(.width(32)) adder_3 (.a(multiplier_5_out), .b(multiplier_6_out), .out(r12));  // open: cin, cout
  Adder #(.width(32)) adder_4 (.a(multiplier_7_out), .b(multiplier_8_out), .out(r22));  // open: cin, cout
endmodule

module maxtrix_mux (
  input  [31:0] a11,
  input  [31:0] b11,
  input  [31:0] a12,
  input  [31:0] b12,
  input  [31:0] a21,
  input  [31:0] b21,
  input  [31:0] a22,
  input  [31:0] b22,
  input  in_9,
  output [31:0] r11,
  output [31:0] r12,
  output [31:0] r21,
  output [31:0] r22
);

  Multiplexer #(.width(32)) multiplexer_1 (.in0(a11), .in1(b11), .out(r11), .sel(in_9));  // open: en
  Multiplexer #(.width(32)) multiplexer_2 (.in0(a12), .in1(b12), .out(r12), .sel(in_9));  // open: en
  Multiplexer #(.width(32)) multiplexer_3 (.in0(a21), .in1(b21), .out(r21), .sel(in_9));  // open: en
  Multiplexer #(.width(32)) multiplexer_4 (.in0(a22), .in1(b22), .out(r22), .sel(in_9));  // open: en

  // Other names for the same wires on the sheet: select = in_9
endmodule

module Init_matrix (
  output [31:0] r11,
  output [31:0] r12,
  output [31:0] r21,
  output [31:0] r22
);


  assign r11 = 32'h1;
  assign r12 = 32'h1;
  assign r21 = 32'h1;
  assign r22 = {32{1'b0}};
endmodule

module E_matrix (
  output [31:0] r11,
  output [31:0] r12,
  output [31:0] r21,
  output [31:0] r22
);


  assign r11 = 32'h1;
  assign r12 = {32{1'b0}};
  assign r21 = {32{1'b0}};
  assign r22 = 32'h1;
endmodule

module calculate (
  input  lowest,
  input  stop,
  output [31:0] Nth
);

  wire clock, control, enable;
  wire [31:0] a11, a12, a21, a22, A_A_r11, A_A_r12, A_A_r21, A_A_r22, E_2_r11, E_2_r12, E_2_r21, E_2_r22,
       E_r11, E_r12, E_r21, E_r22, Init_r11, Init_r12, Init_r21, Init_r22, Mux_2_r11, Mux_2_r12, Mux_2_r21,
       Mux_2_r22, Mux_3_r11, Mux_3_r12, Mux_3_r21, Mux_3_r22, Mux_r11, Mux_r12, Mux_r21, Mux_r22, r11, r12,
       r21, r22, R_N_r11, R_N_r12, R_N_r21, R_N_r22;

  Clock clock_1 (.out(clock));
  Counter #(.width(1), .max('h1), .ongoal("stay")) counter_1 (
    .Q(control), .clk(clock));  // open: load, D, count, carry, clr
  not not_1 (enable, stop);
  E_matrix E (.r11(E_r11), .r12(E_r12), .r21(E_r21), .r22(E_r22));
  maxtrix_mux Mux (
    .a11(E_r11), .b11(a11), .r11(Mux_r11), .a12(E_r12), .b12(a12), .r12(Mux_r12), .a21(E_r21), .b21(a21),
    .r21(Mux_r21), .a22(E_r22), .b22(a22), .r22(Mux_r22), .in_9(lowest));
  matrix_mul A_A (
    .a11(a11), .b11(a11), .r11(A_A_r11), .a12(a12), .b12(a12), .r12(A_A_r12), .a21(a21), .b21(a21),
    .r21(A_A_r21), .a22(a22), .b22(a22), .r22(A_A_r22));
  Init_matrix Init (.r11(Init_r11), .r12(Init_r12), .r21(Init_r21), .r22(Init_r22));
  matrix_mul R_N (
    .a11(r11), .b11(Mux_r11), .r11(R_N_r11), .a12(r12), .b12(Mux_r12), .r12(R_N_r12), .a21(r21),
    .b21(Mux_r21), .r21(R_N_r21), .a22(r22), .b22(Mux_r22), .r22(R_N_r22));
  maxtrix_mux Mux_2 (
    .a11(Init_r11), .b11(A_A_r11), .r11(Mux_2_r11), .a12(Init_r12), .b12(A_A_r12), .r12(Mux_2_r12),
    .a21(Init_r21), .b21(A_A_r21), .r21(Mux_2_r21), .a22(Init_r22), .b22(A_A_r22), .r22(Mux_2_r22),
    .in_9(control));
  matrix_memory A (
    .a11_i(Mux_2_r11), .a11_o(a11), .a12_i(Mux_2_r12), .a12_o(a12), .a21_i(Mux_2_r21), .a21_o(a21),
    .a22_i(Mux_2_r22), .a22_o(a22), .clock(clock), .enable(enable));
  E_matrix E_2 (.r11(E_2_r11), .r12(E_2_r12), .r21(E_2_r21), .r22(E_2_r22));
  Multiplexer #(.width(32)) multiplexer_1 (.in0({32{1'b0}}), .in1(r12), .out(Nth), .sel(stop));  // open: en
  maxtrix_mux Mux_3 (
    .a11(E_2_r11), .b11(R_N_r11), .r11(Mux_3_r11), .a12(E_2_r12), .b12(R_N_r12), .r12(Mux_3_r12),
    .a21(E_2_r21), .b21(R_N_r21), .r21(Mux_3_r21), .a22(E_2_r22), .b22(R_N_r22), .r22(Mux_3_r22),
    .in_9(control));
  matrix_memory R (
    .a11_i(Mux_3_r11), .a11_o(r11), .a12_i(Mux_3_r12), .a12_o(r12), .a21_i(Mux_3_r21), .a21_o(r21),
    .a22_i(Mux_3_r22), .a22_o(r22), .clock(clock), .enable(enable));
endmodule

module count (
  input  [31:0] \input ,
  output lowest,
  output stop
);

  wire clock, comparator_1_eq, control;
  wire [31:0] multiplexer_1_out, num, shifter_1_out;

  Clock clock_1 (.out(clock));
  Counter #(.width(1), .max('h1), .ongoal("stay")) counter_1 (
    .Q(control), .clk(clock));  // open: load, D, count, carry, clr
  Shifter #(.width(32), .shift("lr")) shifter_1 (.in(num), .\dist (5'b00001), .out(shifter_1_out));
  Comparator #(.width(32), .mode("unsigned")) comparator_1 (
    .a(num), .b({32{1'b0}}), .eq(comparator_1_eq));  // open: gt, lt
  Bit_Extender #(.in_width(32), .out_width(1)) bit_extender_1 (.in(num), .out(lowest));
  Multiplexer #(.width(32)) multiplexer_1 (
    .in0(\input ), .in1(shifter_1_out), .out(multiplexer_1_out), .sel(control));  // open: en
  Multiplexer multiplexer_2 (.in0(1'b0), .in1(comparator_1_eq), .out(stop), .sel(control));  // open: en
  Register #(.width(32)) register_1 (.D(multiplexer_1_out), .Q(num), .clk(clock));  // open: en, clr
endmodule
